# Fritzing sketch 0.5.0_Collector (saved by Fritzing 0.9.3b)
circuit board: 5cm x 7cm
breadboards: 1

parts:
  D1M = WeMos D1 Mini
  AM2302 = AM2302 Humidity and Temperature Sensor
  MO1 = Basic Flex Resistor

nets:
  3V3: D1M.3V3, AM2302.VDD
  N1: D1M.A0, MO1.Pin_2
  N2: D1M.D3, MO1.pin_1
  N3: D1M.D7, AM2302.DATA
  N4: D1M.G, AM2302.GND
